// Logisim project ProjectCA.circ as structural Verilog: 11 circuits, main circuit main
module ALU (
  input  [31:0] Read_data_1,
  input  [31:0] Input2,
  input  CarryIn_Addi,
  input  [2:0] SelectionOfALUMux,
  input  [31:0] AddiSecondInpit,
  input  CarryInAdd,
  input  CarryInSUB,
  output [31:0] ALU_result,
  output CarryOut_Addi,
  output CarryoutAdd,
  output CarryOutSub,
  output GreaterThan,
  output ZeroFlag
);

  wire comparator_1_lt;
  wire [31:0] adder_1_out, adder_2_out, AND_out, bit_extender_1_out, OR_out, subtractor_1_out;

  assign AND_out = Read_data_1 & Input2;  // AND_Gate AND, 32 bits wide
  assign OR_out = Read_data_1 | Input2;  // OR_Gate OR, 32 bits wide
  Adder #(.width(32)) adder_1 (
    .a(Read_data_1), .b(AddiSecondInpit), .out(adder_1_out), .cin(CarryIn_Addi), .cout(CarryOut_Addi));
  Adder #(.width(32)) adder_2 (.a(Read_data_1), .b(Input2), .out(adder_2_out), .cin(CarryInAdd), .cout(CarryoutAdd));
  Subtractor #(.width(32)) subtractor_1 (
    .a(Read_data_1), .b(Input2), .out(subtractor_1_out), .bin(CarryInSUB), .bout(CarryOutSub));
  Comparator #(.width(32)) comparator_1 (
    .a(Read_data_1), .b(Input2), .gt(GreaterThan), .eq(ZeroFlag), .lt(comparator_1_lt));
  assign bit_extender_1_out = {{31{1'b0}}, comparator_1_lt};  // Bit_Extender bit_extender_1
  Multiplexer #(.select(3), .width(32), .enable("false")) multiplexer_1 (
    .in0(AND_out), .in1(OR_out), .in2(adder_1_out), .in3(adder_2_out), .in4(subtractor_1_out),
    .in5(bit_extender_1_out), .out(ALU_result), .sel(SelectionOfALUMux));  // open: in6, in7
endmodule

// ControlUniit
module Control_Unit (
  input  Op5,
  input  op4,
  input  op3,
  input  op2,
  input  op1,
  input  op0,
  output RegDst,
  output Branch,
  output MemRead,
  output MemToReg,
  output ALUOp1,
  output ALUOp0,
  output MemWrite,
  output ALUSrc,
  output RegWrite
);

  wire ALUSrc_addi, not_1_out, not_2_out, not_3_out, not_4_out, not_5_out, not_6_out;

  not not_1 (not_1_out, Op5);
  not not_2 (not_2_out, op4);
  not not_3 (not_3_out, op3);
  not not_4 (not_4_out, op2);
  not not_5 (not_5_out, op1);
  not not_6 (not_6_out, op0);
  and R_format (ALUOp1, not_1_out, not_2_out, not_3_out, not_4_out, not_5_out, not_6_out);
  and Load (MemRead, Op5, not_2_out, not_3_out, not_4_out, op1, op0);
  and Store (MemWrite, Op5, not_2_out, op3, not_4_out, op1, op0);
  and Beq (ALUOp0, not_1_out, not_2_out, not_3_out, op2, not_5_out, not_6_out);
  or or_1 (ALUSrc, MemWrite, MemRead, ALUSrc_addi);
  or or_2 (RegWrite, MemRead, ALUOp1, ALUSrc_addi);
  and Addi (ALUSrc_addi, not_1_out, not_2_out, op3, not_4_out, not_5_out, not_6_out);
  buf or_3 (RegDst, ALUOp1);  // OR_Gate

  assign Branch = ALUOp0;
  assign MemToReg = MemRead;
endmodule

// DataMemory
module Data_memory (
  input  [31:0] Data_In,
  input  [23:0] Address,
  input  Reset,
  input  MemWrite,
  input  MemRead,
  output [31:0] Data_Out
);

  wire clock_1_out;

  Clock clock_1 (.out(clock_1_out));
  RAM #(.addrWidth(24), .dataWidth(32), .bus("separate")) ram_1 (
    .addr(Address), .din(Data_In), .data(Data_Out), .str(MemWrite), .sel(1'b1), .clk(clock_1_out),
    .ld(MemRead), .clr(Reset));
endmodule

module Instruction_memory (
  input  [23:0] PC,
  output [31:0] InstructionMemoOutput
);

  ROM #(.addrWidth(24), .dataWidth(32)) rom_1 (.addr(PC), .data(InstructionMemoOutput), .sel(1'b1));
endmodule

// RegisterFile
module Register_File (
  input  RegWrite,
  input  [4:0] Write_Register,
  input  [4:0] Read_Register_1,
  input  [4:0] Read_Register_2,
  input  [31:0] Write_Data,
  output [31:0] Read_Data_1,
  output [31:0] Read_Data_2
);

  wire Clk, En0, En1, En2, En3, En4, En5, En6, En7, En8, En9, En10, En11, En12, En13, En14, En15, En16, En17,
       En18, En19, En20, En21, En22, En23, En24, En25, En26, En27, En28, En29, En30, En31;
  wire [31:0] Reg0, Reg1, Reg2, Reg3, Reg4, Reg5, Reg6, Reg7, Reg8, Reg9, Reg10, Reg11, Reg12, Reg13, Reg14,
       Reg15, Reg16, Reg17, Reg18, Reg19, Reg20, Reg21, Reg22, Reg23, Reg24, Reg25, Reg26, Reg27, Reg28,
       Reg29, Reg30, Reg31;

  Clock clock_1 (.out(Clk));
  Register #(.width(32)) register_1 (.D({32{1'b0}}), .en(En0), .Q(Reg0), .clk(Clk));  // open: clr
  Register #(.width(32)) register_2 (.D(Write_Data), .en(En1), .Q(Reg1), .clk(Clk));  // open: clr
  Register #(.width(32)) register_3 (.D(Write_Data), .en(En2), .Q(Reg2), .clk(Clk));  // open: clr
  Register #(.width(32)) register_4 (.D(Write_Data), .en(En3), .Q(Reg3), .clk(Clk));  // open: clr
  Register #(.width(32)) register_5 (.D(Write_Data), .en(En4), .Q(Reg4), .clk(Clk));  // open: clr
  Register #(.width(32)) register_6 (.D(Write_Data), .en(En5), .Q(Reg5), .clk(Clk));  // open: clr
  Register #(.width(32)) register_7 (.D(Write_Data), .en(En6), .Q(Reg6), .clk(Clk));  // open: clr
  Register #(.width(32)) register_8 (.D(Write_Data), .en(En7), .Q(Reg7), .clk(Clk));  // open: clr
  Register #(.width(32)) register_9 (.D(Write_Data), .en(En8), .Q(Reg8), .clk(Clk));  // open: clr
  Register #(.width(32)) register_10 (.D(Write_Data), .en(En9), .Q(Reg9), .clk(Clk));  // open: clr
  Register #(.width(32)) register_11 (.D(Write_Data), .en(En10), .Q(Reg10), .clk(Clk));  // open: clr
  Register #(.width(32)) register_12 (.D(Write_Data), .en(En11), .Q(Reg11), .clk(Clk));  // open: clr
  Register #(.width(32)) register_13 (.D(Write_Data), .en(En12), .Q(Reg12), .clk(Clk));  // open: clr
  Register #(.width(32)) register_14 (.D(Write_Data), .en(En13), .Q(Reg13), .clk(Clk));  // open: clr
  Register #(.width(32)) register_15 (.D(Write_Data), .en(En14), .Q(Reg14), .clk(Clk));  // open: clr
  Register #(.width(32)) register_16 (.D(Write_Data), .en(En15), .Q(Reg15), .clk(Clk));  // open: clr
  Register #(.width(32)) register_17 (.D(Write_Data), .en(En16), .Q(Reg16), .clk(Clk));  // open: clr
  Register #(.width(32)) register_18 (.D(Write_Data), .en(En17), .Q(Reg17), .clk(Clk));  // open: clr
  Register #(.width(32)) register_19 (.D(Write_Data), .en(En18), .Q(Reg18), .clk(Clk));  // open: clr
  Register #(.width(32)) register_20 (.D(Write_Data), .en(En19), .Q(Reg19), .clk(Clk));  // open: clr
  Register #(.width(32)) register_21 (.D(Write_Data), .en(En20), .Q(Reg20), .clk(Clk));  // open: clr
  Register #(.width(32)) register_22 (.D(Write_Data), .en(En21), .Q(Reg21), .clk(Clk));  // open: clr
  Register #(.width(32)) register_23 (.D(Write_Data), .en(En22), .Q(Reg22), .clk(Clk));  // open: clr
  Register #(.width(32)) register_24 (.D(Write_Data), .en(En23), .Q(Reg23), .clk(Clk));  // open: clr
  Register #(.width(32)) register_25 (.D(Write_Data), .en(En24), .Q(Reg24), .clk(Clk));  // open: clr
  Register #(.width(32)) register_26 (.D(Write_Data), .en(En25), .Q(Reg25), .clk(Clk));  // open: clr
  Register #(.width(32)) register_27 (.D(Write_Data), .en(En26), .Q(Reg26), .clk(Clk));  // open: clr
  Register #(.width(32)) register_28 (.D(Write_Data), .en(En27), .Q(Reg27), .clk(Clk));  // open: clr
  Register #(.width(32)) register_29 (.D(Write_Data), .en(En28), .Q(Reg28), .clk(Clk));  // open: clr
  Register #(.width(32)) register_30 (.D(Write_Data), .en(En29), .Q(Reg29), .clk(Clk));  // open: clr
  Register #(.width(32)) register_31 (.D(Write_Data), .en(En30), .Q(Reg30), .clk(Clk));  // open: clr
  Register #(.width(32)) register_32 (.D(Write_Data), .en(En31), .Q(Reg31), .clk(Clk));  // open: clr
  Decoder #(.select(5), .disabled(0)) decoder_1 (
    .out0(En0), .out1(En1), .out2(En2), .out3(En3), .out4(En4), .out5(En5), .out6(En6), .out7(En7),
    .out8(En8), .out9(En9), .out10(En10), .out11(En11), .out12(En12), .out13(En13), .out14(En14),
    .out15(En15), .out16(En16), .out17(En17), .out18(En18), .out19(En19), .out20(En20), .out21(En21),
    .out22(En22), .out23(En23), .out24(En24), .out25(En25), .out26(En26), .out27(En27), .out28(En28),
    .out29(En29), .out30(En30), .out31(En31), .sel(Write_Register), .en(RegWrite));
  Multiplexer #(.select(5), .width(32), .enable("false")) multiplexer_1 (
    .in0(Reg0), .in1(Reg1), .in2(Reg2), .in3(Reg3), .in4(Reg4), .in5(Reg5), .in6(Reg6), .in7(Reg7),
    .in8(Reg8), .in9(Reg9), .in10(Reg10), .in11(Reg11), .in12(Reg12), .in13(Reg13), .in14(Reg14),
    .in15(Reg15), .in16(Reg16), .in17(Reg17), .in18(Reg18), .in19(Reg19), .in20(Reg20), .in21(Reg21),
    .in22(Reg22), .in23(Reg23), .in24(Reg24), .in25(Reg25), .in26(Reg26), .in27(Reg27), .in28(Reg28),
    .in29(Reg29), .in30(Reg30), .in31(Reg31), .out(Read_Data_1), .sel(Read_Register_1));
  Multiplexer #(.select(5), .width(32), .enable("false")) multiplexer_2 (
    .in0(Reg0), .in1(Reg1), .in2(Reg2), .in3(Reg3), .in4(Reg4), .in5(Reg5), .in6(Reg6), .in7(Reg7),
    .in8(Reg8), .in9(Reg9), .in10(Reg10), .in11(Reg11), .in12(Reg12), .in13(Reg13), .in14(Reg14),
    .in15(Reg15), .in16(Reg16), .in17(Reg17), .in18(Reg18), .in19(Reg19), .in20(Reg20), .in21(Reg21),
    .in22(Reg22), .in23(Reg23), .in24(Reg24), .in25(Reg25), .in26(Reg26), .in27(Reg27), .in28(Reg28),
    .in29(Reg29), .in30(Reg30), .in31(Reg31), .out(Read_Data_2), .sel(Read_Register_2));

  // Other names for the same wires on the sheet: WData[31:0] = Write_Data
endmodule

module main (
  input  in_1,
  input  in_2,
  input  in_3,
  input  [4:0] in_4,
  input  in_5,
  input  in_6,
  input  in_7,
  input  in_8,
  input  in_9,
  input  in_10,
  input  in_11,
  input  in_12,
  input  in_13,
  input  [4:0] in_14,
  input  [31:0] in_15,
  input  in_16,
  input  in_17,
  input  in_18,
  input  [31:0] in_19,
  input  in_20,
  input  in_21,
  output out_22,
  output out_23,
  output out_24,
  output out_25
);

  wire ALU_Op0, ALU_Op0_ID_EX, ALU_Op1, ALU_Op1_ID_EX, ALUSrc, ALUSrc_ID_EX, Branch, Branch_ID_EX,
       clock_1_out, MemRead, MemRead_ID_EX, MemToReg, MemToReg_ID_EX, MemWrite, MemWrite_ID_EX,
       multiplexer_5_out, Output1RegWriteMEM_WB, Output2MEMToRegMEM_WB, Output_M_Branch_EX_MEM,
       Output_M_MemRead_EX_MEM, Output_M_MemWrite_EX_MEM, Output_WB_MEMtoReg_EX_MEM,
       Output_WB_RegWrite_EX_MEM, RegDst, RegDst_ID_EX, RegWrite, RegWrite_ID_EX, SelectionOfBranchMux,
       Zero_Flag_Output_EX_MEM, ZeroFlag;
  wire [2:0] SelectionALUMux;
  wire [4:0] I_15_11_ID_EX, I_20_16, I_20_16_ID_EX, I_25_21, multiplexer_3_out,
       Output5writeRegOutput_Mux_MEM_WB, Output_writeRegMuxOutput_EX_MEM, writeRegMuxOutput;
  wire [5:0] I_31_26;
  wire [15:0] I_15_0;
  wire [23:0] BranchOutput, OutputFirstAdd, PC;
  wire [31:0] ALU_result, DataMemMuxOutput, Input2OfAluMux, input2OfIF_ID, multiplexer_7_out, output1OfIF_ID,
       output1OfIF_ID_ID_EX, Output3_ReadData_MENM_WB, Output_4_ALU_Result_MEM_WB, Output_ALU_Result_EX_MEM,
       Output_secondAdd_EX_MEM, OutputFirstAdd32, OutputReadData2_EX_MEM, OutputSecondAdd, Read_data,
       ReadData1, ReadData1_ID_EX, ReadData2, ReadData2_ID_EX, shifter_1_out, SignBitExtender,
       SignBitExtender_ID_EX;
  wire [31:24] multiplexer_4_out;

  assign SignBitExtender = {{16{1'b0}}, I_15_0};  // Bit_Extender bit_extender_1
  Control_Unit control_unit_1 (
    .Op5(I_31_26[5]), .op4(I_31_26[4]), .op3(I_31_26[3]), .op2(I_31_26[2]), .op1(I_31_26[1]),
    .op0(I_31_26[0]), .RegDst(RegDst), .Branch(Branch), .MemRead(MemRead), .MemToReg(MemToReg),
    .ALUOp1(ALU_Op1), .ALUOp0(ALU_Op0), .MemWrite(MemWrite), .ALUSrc(ALUSrc), .RegWrite(RegWrite));
  Register #(.width(24)) register_1 (.D(BranchOutput), .en(in_16), .Q(PC), .clk(clock_1_out), .clr(in_17));
  Clock clock_1 (.out(clock_1_out));
  Adder #(.width(24)) adder_1 (.a(24'h1), .b(PC), .out(OutputFirstAdd), .cin(in_3), .cout(in_5));
  Multiplexer #(.width(32), .enable("false")) multiplexer_1 (
    .in0(ReadData2_ID_EX), .in1(SignBitExtender_ID_EX), .out(Input2OfAluMux), .sel(ALUSrc_ID_EX));
  ROM #(.addrWidth(24), .dataWidth(32)) rom_1 (.addr(PC), .data(input2OfIF_ID), .sel(1'b1));
  Data_memory data_memory_1 (
    .Data_In(OutputReadData2_EX_MEM), .Address(Output_ALU_Result_EX_MEM[23:0]), .Data_Out(Read_data),
    .Reset(in_21), .MemWrite(Output_M_MemWrite_EX_MEM), .MemRead(Output_M_MemRead_EX_MEM));
  IF_ID if_id_1 (
    .Input1IF_ID(OutputFirstAdd32), .Input2IF_ID(input2OfIF_ID), .enable1(in_6), .enable3(in_8), .in_3(in_9),
    .in_6(in_7), .Output1IF_ID(output1OfIF_ID), .Output2IF_ID({I_31_26, I_25_21, I_20_16, I_15_0}));
  Multiplexer #(.width(5), .enable("false")) multiplexer_2 (
    .in0(I_20_16_ID_EX), .in1(I_15_11_ID_EX), .out(writeRegMuxOutput), .sel(RegDst_ID_EX));
  assign OutputFirstAdd32 = {{8{1'b0}}, OutputFirstAdd};  // Bit_Extender bit_extender_2
  ALU_control alu_control_1 (
    .ALUOp1(ALU_Op1_ID_EX), .ALUOp0(ALU_Op0_ID_EX), .F5(SignBitExtender_ID_EX[5]),
    .F4(SignBitExtender_ID_EX[4]), .F3(SignBitExtender_ID_EX[3]), .F2(SignBitExtender_ID_EX[2]),
    .F1(SignBitExtender_ID_EX[1]), .F0(SignBitExtender_ID_EX[0]), .Operation0(SelectionALUMux[2]),
    .Operation1(SelectionALUMux[1]), .Operation2(SelectionALUMux[0]));
  MEM_WB mem_wb_1 (
    .WB_MEM_WB1(Output_WB_RegWrite_EX_MEM), .WB_MEM_WB2(Output_WB_MEMtoReg_EX_MEM),
    .Read_data_MEM_WB(Read_data), .ALU_result_MEM_WB(Output_ALU_Result_EX_MEM),
    .WriteregMuxoutput_MEM_WB(Output_writeRegMuxOutput_EX_MEM), .enable5(1'b1), .enable3(1'b1),
    .enable1(1'b1), .enable2(1'b1), .enable4(1'b1), .Output_WB_MEM_WB1(Output1RegWriteMEM_WB),
    .Output_WB_MEM_WB2(Output2MEMToRegMEM_WB), .Read_data_MEM_WB_2(Output3_ReadData_MENM_WB),
    .Output_ALU_resultMEM_WB(Output_4_ALU_Result_MEM_WB),
    .Output_WriteregMuxoutput_MEM_WB(Output5writeRegOutput_Mux_MEM_WB));  // open: in_6, in_12, in_3, in_9, in_15
  Shifter #(.width(32)) shifter_1 (.in(SignBitExtender_ID_EX), .\dist (in_4), .out(shifter_1_out));
  Adder #(.width(32)) adder_2 (.a(output1OfIF_ID_ID_EX), .b(shifter_1_out), .out(OutputSecondAdd));  // open: cin, cout
  Multiplexer #(.width(5), .enable("false")) multiplexer_3 (
    .in0(in_14), .in1(Output5writeRegOutput_Mux_MEM_WB), .out(multiplexer_3_out), .sel(in_18));
  Multiplexer #(.width(32), .enable("false")) multiplexer_4 (
    .in0(OutputFirstAdd32), .in1(Output_secondAdd_EX_MEM), .out({multiplexer_4_out, BranchOutput}),
    .sel(SelectionOfBranchMux));
  Multiplexer #(.enable("false")) multiplexer_5 (
    .in0(1'b1), .in1(Output1RegWriteMEM_WB), .out(multiplexer_5_out), .sel(in_10));
  Register_File register_file_1 (
    .RegWrite(multiplexer_5_out), .Read_Data_1(ReadData1), .Read_Data_2(ReadData2),
    .Write_Data(multiplexer_7_out), .Read_Register_1(I_25_21), .Read_Register_2(I_20_16),
    .Write_Register(multiplexer_3_out));
  Multiplexer #(.width(32), .enable("false")) multiplexer_6 (
    .in0(Output_4_ALU_Result_MEM_WB), .in1(Output3_ReadData_MENM_WB), .out(DataMemMuxOutput),
    .sel(Output2MEMToRegMEM_WB));
  Multiplexer #(.width(32), .enable("false")) multiplexer_7 (
    .in0(in_19), .in1(DataMemMuxOutput), .out(multiplexer_7_out), .sel(in_20));
  ALU alu_1 (
    .Read_data_1(ReadData1_ID_EX), .Input2(Input2OfAluMux), .AddiSecondInpit(in_15), .CarryInAdd(in_11),
    .CarryInSUB(in_12), .CarryIn_Addi(in_13), .CarryoutAdd(out_23), .CarryOutSub(out_24),
    .CarryOut_Addi(out_25), .SelectionOfALUMux(SelectionALUMux), .ALU_result(ALU_result),
    .GreaterThan(out_22), .ZeroFlag(ZeroFlag));
  and and_1 (SelectionOfBranchMux, Zero_Flag_Output_EX_MEM, Output_M_Branch_EX_MEM);
  ID_EX id_ex_1 (
    .WB_RegWrite_ID_EX(RegWrite), .WB_MemtoReg_ID_EX(MemToReg), .M_MemWrite_ID_EX(MemWrite),
    .M_MemRead_ID_EX(MemRead), .M_Branch_ID_EX(Branch), .EX_ALUOp0_ID_EX(ALU_Op0), .EX_ALUOp1_ID_EX(ALU_Op1),
    .EX_ALUSrc_ID_EX(ALUSrc), .EX__RegDest_ID_EX(RegDst), .Input4ID_EX(output1OfIF_ID),
    .Read_data1_ID_EX(ReadData1), .Read_data2_ID_EX(ReadData2), .Sign_extend_ID_EX(SignBitExtender),
    .I_20_16_ID_EX(I_20_16), .I_15_11_ID_EX(I_15_0[15:11]), .enable5(1'b1), .enable4(1'b1), .enable2(1'b1),
    .enable3(1'b1), .enable6(1'b1), .enable8(1'b1), .enable1(1'b1), .enable7(1'b1), .enable9(1'b1),
    .enable11(1'b1), .enable12(1'b1), .enable14(1'b1), .enable10(1'b1), .enable13(1'b1), .enable15(1'b1),
    .OutputWB_RegWrite_ID_EX(RegWrite_ID_EX), .OutputWB_MemtoReg_ID_EX(MemToReg_ID_EX),
    .OutputM_MemWrite_ID_EX(MemWrite_ID_EX), .OutputM_MemRead_ID_EX(MemRead_ID_EX),
    .OutputM_Branch_ID_EX(Branch_ID_EX), .OutputEX_ALUOp0_ID_EX(ALU_Op0_ID_EX),
    .OutputEX_ALUOp1ID_EX(ALU_Op1_ID_EX), .OutputEX_ALUSrc_ID_EX(ALUSrc_ID_EX),
    .OutputEX__RegDestID_EX(RegDst_ID_EX), .Output4ID_EX(output1OfIF_ID_ID_EX),
    .Output_Read_data1_ID_EX(ReadData1_ID_EX), .Output_Read_data2_ID_EX(ReadData2_ID_EX),
    .Output_Sign_extend_ID_EX(SignBitExtender_ID_EX), .Output_I_20_16_ID_EX(I_20_16_ID_EX),
    .Output_I_15_11_ID_EX(I_15_11_ID_EX));  // open: in_15, in_12, in_6, in_9, in_18, in_24, in_3, in_21, in_27, in_33, in_36, in_42, in_30, in_39, in_45
  EX_MEM ex_mem_1 (
    .WB_RegWrite_EX_MEM(RegWrite_ID_EX), .WB_MemtoReg_EX_MEM(MemToReg_ID_EX),
    .M_MemWrite_EX_MEM(MemWrite_ID_EX), .M_MemRead_EX_MEM(MemRead_ID_EX), .SecondAdd_EX_MEM(OutputSecondAdd),
    .M_Branch_EX_MEM(Branch_ID_EX), .ZeroFlag_EX_MEM(ZeroFlag), .ALU_result_EX_MEM(ALU_result),
    .Read_data2_EX_MEM(ReadData2_ID_EX), .Input7_EX_MEM(writeRegMuxOutput), .enable1(1'b1), .enable2(1'b1),
    .enable3(1'b1), .enable5(1'b1), .enable6(1'b1), .enable7(1'b1), .enable8(1'b1), .enable4(1'b1),
    .enable9(1'b1), .enable10(1'b1), .OutputWB_RegWrite_EX_MEM(Output_WB_RegWrite_EX_MEM),
    .OutputWB_MemtoReg_EX_MEM(Output_WB_MEMtoReg_EX_MEM), .OutputM_MemWrite_EX_MEM(Output_M_MemWrite_EX_MEM),
    .OutputM_MemRead_EX_MEM(Output_M_MemRead_EX_MEM), .Output_secondAdd_EX_MEM(Output_secondAdd_EX_MEM),
    .OutputM_Branch_EX_MEM(Output_M_Branch_EX_MEM), .Output_ZeroFlag_EX_MEM(Zero_Flag_Output_EX_MEM),
    .Output_ALU_result_EX_MEM(Output_ALU_Result_EX_MEM), .Output_Read_data2_EX_MEM(OutputReadData2_EX_MEM),
    .Output7EX_MEM(Output_writeRegMuxOutput_EX_MEM));  // open: in_3, in_6, in_9, in_15, in_18, in_21, in_24, in_12, in_27, in_30

  // Other names for the same wires on the sheet: output2OfIF_ID[31:0] = {I_31_26, I_25_21, I_20_16, I_15_0};
  //   I_15_11[4:0] = I_15_0[15:11]

  // Notes on the sheet:
  //   contents of rom_1 (hex, n*v repeats v):
  //   2119020 1230fffc 3402000a c
endmodule

// ALU Control
module ALU_control (
  input  ALUOp1,
  input  ALUOp0,
  input  F5,
  input  F4,
  input  F3,
  input  F2,
  input  F1,
  input  F0,
  output Operation0,
  output Operation1,
  output Operation2
);

  wire and_1_out, and_2_out, and_3_out, and_4_out, and_5_out, and_6_out, and_7_out, and_8_out, not_1_out,
       not_2_out, not_3_out, not_4_out, not_5_out, not_6_out, not_7_out, not_8_out, not_9_out, not_10_out,
       not_11_out, not_12_out, not_13_out, not_14_out;

  not not_1 (not_1_out, F2);
  and and_1 (and_1_out, ALUOp1, not_1_out, F1);
  not not_2 (not_2_out, ALUOp1);
  and and_2 (and_2_out, not_2_out, not_3_out);
  not not_3 (not_3_out, ALUOp0);
  not not_4 (not_4_out, ALUOp0);
  and and_3 (and_3_out, not_4_out, F1, F0);
  and and_4 (and_4_out, ALUOp1, not_5_out, not_6_out);
  not not_5 (not_5_out, F2);
  not not_6 (not_6_out, F1);
  not not_7 (not_7_out, ALUOp1);
  and and_5 (and_5_out, not_7_out, not_8_out);
  not not_8 (not_8_out, ALUOp0);
  not not_9 (not_9_out, ALUOp0);
  and and_6 (and_6_out, not_9_out, not_10_out, not_11_out);
  not not_10 (not_10_out, F2);
  not not_11 (not_11_out, F1);
  not not_12 (not_12_out, ALUOp0);
  not not_13 (not_13_out, F1);
  and and_7 (and_7_out, not_12_out, not_13_out, F0);
  not not_14 (not_14_out, ALUOp0);
  and and_8 (and_8_out, not_14_out, F3);
  or or_1 (Operation0, ALUOp0, and_1_out);
  or or_2 (Operation1, and_2_out, and_3_out, and_4_out);
  or or_3 (Operation2, and_5_out, and_6_out, and_7_out, and_8_out);
endmodule

module IF_ID (
  input  [31:0] Input1IF_ID,
  input  enable1,
  input  in_3,
  input  [31:0] Input2IF_ID,
  input  enable3,
  input  in_6,
  output [31:0] Output1IF_ID,
  output [31:0] Output2IF_ID
);

  wire Clock_2_out, Clock_out;

  Clock Clock (.out(Clock_out));
  Clock Clock_2 (.out(Clock_2_out));
  Register #(.width(32)) register_1 (.D(Input1IF_ID), .en(enable1), .Q(Output1IF_ID), .clk(Clock_out), .clr(in_3));
  Register #(.width(32)) register_2 (.D(Input2IF_ID), .en(enable3), .Q(Output2IF_ID), .clk(Clock_2_out), .clr(in_6));
endmodule

module ID_EX (
  input  WB_RegWrite_ID_EX,
  input  enable1,
  input  in_3,
  input  WB_MemtoReg_ID_EX,
  input  enable2,
  input  in_6,
  input  M_MemWrite_ID_EX,
  input  enable3,
  input  in_9,
  input  M_MemRead_ID_EX,
  input  enable4,
  input  in_12,
  input  M_Branch_ID_EX,
  input  enable5,
  input  in_15,
  input  EX_ALUOp0_ID_EX,
  input  enable6,
  input  in_18,
  input  EX_ALUOp1_ID_EX,
  input  enable7,
  input  in_21,
  input  EX_ALUSrc_ID_EX,
  input  enable8,
  input  in_24,
  input  EX__RegDest_ID_EX,
  input  enable9,
  input  in_27,
  input  [31:0] Input4ID_EX,
  input  enable10,
  input  in_30,
  input  [31:0] Read_data1_ID_EX,
  input  enable11,
  input  in_33,
  input  [31:0] Read_data2_ID_EX,
  input  enable12,
  input  in_36,
  input  [31:0] Sign_extend_ID_EX,
  input  enable13,
  input  in_39,
  input  [4:0] I_20_16_ID_EX,
  input  enable14,
  input  in_42,
  input  [4:0] I_15_11_ID_EX,
  input  enable15,
  input  in_45,
  output OutputWB_RegWrite_ID_EX,
  output OutputWB_MemtoReg_ID_EX,
  output OutputM_MemWrite_ID_EX,
  output OutputM_MemRead_ID_EX,
  output OutputM_Branch_ID_EX,
  output OutputEX_ALUOp0_ID_EX,
  output OutputEX_ALUOp1ID_EX,
  output OutputEX_ALUSrc_ID_EX,
  output OutputEX__RegDestID_EX,
  output [31:0] Output4ID_EX,
  output [31:0] Output_Read_data1_ID_EX,
  output [31:0] Output_Read_data2_ID_EX,
  output [31:0] Output_Sign_extend_ID_EX,
  output [4:0] Output_I_20_16_ID_EX,
  output [4:0] Output_I_15_11_ID_EX
);

  wire clock_1_out, clock_2_out, clock_3_out, clock_4_out, clock_5_out, clock_6_out, clock_7_out,
       clock_8_out, clock_9_out, clock_10_out, clock_11_out, clock_12_out, clock_13_out, clock_14_out,
       clock_15_out;

  Register #(.width(1)) register_1 (
    .D(WB_RegWrite_ID_EX), .en(enable1), .Q(OutputWB_RegWrite_ID_EX), .clk(clock_1_out), .clr(in_3));
  Clock clock_1 (.out(clock_1_out));
  Register #(.width(1)) register_2 (
    .D(WB_MemtoReg_ID_EX), .en(enable2), .Q(OutputWB_MemtoReg_ID_EX), .clk(clock_2_out), .clr(in_6));
  Clock clock_2 (.out(clock_2_out));
  Register #(.width(1)) register_3 (
    .D(M_MemWrite_ID_EX), .en(enable3), .Q(OutputM_MemWrite_ID_EX), .clk(clock_3_out), .clr(in_9));
  Clock clock_3 (.out(clock_3_out));
  Register #(.width(1)) register_4 (
    .D(M_MemRead_ID_EX), .en(enable4), .Q(OutputM_MemRead_ID_EX), .clk(clock_4_out), .clr(in_12));
  Clock clock_4 (.out(clock_4_out));
  Register #(.width(1)) register_5 (
    .D(M_Branch_ID_EX), .en(enable5), .Q(OutputM_Branch_ID_EX), .clk(clock_5_out), .clr(in_15));
  Clock clock_5 (.out(clock_5_out));
  Register #(.width(1)) register_6 (
    .D(EX_ALUOp0_ID_EX), .en(enable6), .Q(OutputEX_ALUOp0_ID_EX), .clk(clock_6_out), .clr(in_18));
  Clock clock_6 (.out(clock_6_out));
  Register #(.width(1)) register_7 (
    .D(EX_ALUOp1_ID_EX), .en(enable7), .Q(OutputEX_ALUOp1ID_EX), .clk(clock_7_out), .clr(in_21));
  Clock clock_7 (.out(clock_7_out));
  Register #(.width(1)) register_8 (
    .D(EX_ALUSrc_ID_EX), .en(enable8), .Q(OutputEX_ALUSrc_ID_EX), .clk(clock_8_out), .clr(in_24));
  Clock clock_8 (.out(clock_8_out));
  Register #(.width(1)) register_9 (
    .D(EX__RegDest_ID_EX), .en(enable9), .Q(OutputEX__RegDestID_EX), .clk(clock_9_out), .clr(in_27));
  Clock clock_9 (.out(clock_9_out));
  Clock clock_10 (.out(clock_10_out));
  Clock clock_11 (.out(clock_11_out));
  Clock clock_12 (.out(clock_12_out));
  Clock clock_13 (.out(clock_13_out));
  Clock clock_14 (.out(clock_14_out));
  Clock clock_15 (.out(clock_15_out));
  Register #(.width(32)) register_10 (
    .D(Input4ID_EX), .en(enable10), .Q(Output4ID_EX), .clk(clock_10_out), .clr(in_30));
  Register #(.width(32)) register_11 (
    .D(Read_data1_ID_EX), .en(enable11), .Q(Output_Read_data1_ID_EX), .clk(clock_11_out), .clr(in_33));
  Register #(.width(32)) register_12 (
    .D(Read_data2_ID_EX), .en(enable12), .Q(Output_Read_data2_ID_EX), .clk(clock_12_out), .clr(in_36));
  Register #(.width(32)) register_13 (
    .D(Sign_extend_ID_EX), .en(enable13), .Q(Output_Sign_extend_ID_EX), .clk(clock_13_out), .clr(in_39));
  Register #(.width(5)) register_14 (
    .D(I_20_16_ID_EX), .en(enable14), .Q(Output_I_20_16_ID_EX), .clk(clock_14_out), .clr(in_42));
  Register #(.width(5)) register_15 (
    .D(I_15_11_ID_EX), .en(enable15), .Q(Output_I_15_11_ID_EX), .clk(clock_15_out), .clr(in_45));
endmodule

module EX_MEM (
  input  WB_RegWrite_EX_MEM,
  input  enable1,
  input  in_3,
  input  WB_MemtoReg_EX_MEM,
  input  enable2,
  input  in_6,
  input  M_MemWrite_EX_MEM,
  input  enable3,
  input  in_9,
  input  M_MemRead_EX_MEM,
  input  enable4,
  input  in_12,
  input  [31:0] SecondAdd_EX_MEM,
  input  enable5,
  input  in_15,
  input  M_Branch_EX_MEM,
  input  enable6,
  input  in_18,
  input  ZeroFlag_EX_MEM,
  input  enable7,
  input  in_21,
  input  [31:0] ALU_result_EX_MEM,
  input  enable8,
  input  in_24,
  input  [31:0] Read_data2_EX_MEM,
  input  enable9,
  input  in_27,
  input  [4:0] Input7_EX_MEM,
  input  enable10,
  input  in_30,
  output OutputWB_RegWrite_EX_MEM,
  output OutputWB_MemtoReg_EX_MEM,
  output OutputM_MemWrite_EX_MEM,
  output OutputM_MemRead_EX_MEM,
  output [31:0] Output_secondAdd_EX_MEM,
  output OutputM_Branch_EX_MEM,
  output Output_ZeroFlag_EX_MEM,
  output [31:0] Output_ALU_result_EX_MEM,
  output [31:0] Output_Read_data2_EX_MEM,
  output [4:0] Output7EX_MEM
);

  wire clock_1_out, clock_2_out, clock_3_out, clock_4_out, clock_5_out, clock_6_out, clock_7_out,
       clock_8_out, clock_9_out, clock_10_out;

  Register #(.width(1)) register_1 (
    .D(WB_RegWrite_EX_MEM), .en(enable1), .Q(OutputWB_RegWrite_EX_MEM), .clk(clock_1_out), .clr(in_3));
  Clock clock_1 (.out(clock_1_out));
  Register #(.width(1)) register_2 (
    .D(WB_MemtoReg_EX_MEM), .en(enable2), .Q(OutputWB_MemtoReg_EX_MEM), .clk(clock_2_out), .clr(in_6));
  Clock clock_2 (.out(clock_2_out));
  Register #(.width(1)) register_3 (
    .D(M_MemWrite_EX_MEM), .en(enable3), .Q(OutputM_MemWrite_EX_MEM), .clk(clock_3_out), .clr(in_9));
  Clock clock_3 (.out(clock_3_out));
  Register #(.width(1)) register_4 (
    .D(M_MemRead_EX_MEM), .en(enable4), .Q(OutputM_MemRead_EX_MEM), .clk(clock_4_out), .clr(in_12));
  Clock clock_4 (.out(clock_4_out));
  Register #(.width(32)) register_5 (
    .D(SecondAdd_EX_MEM), .en(enable5), .Q(Output_secondAdd_EX_MEM), .clk(clock_5_out), .clr(in_15));
  Clock clock_5 (.out(clock_5_out));
  Register #(.width(1)) register_6 (
    .D(M_Branch_EX_MEM), .en(enable6), .Q(OutputM_Branch_EX_MEM), .clk(clock_6_out), .clr(in_18));
  Clock clock_6 (.out(clock_6_out));
  Register #(.width(1)) register_7 (
    .D(ZeroFlag_EX_MEM), .en(enable7), .Q(Output_ZeroFlag_EX_MEM), .clk(clock_7_out), .clr(in_21));
  Clock clock_7 (.out(clock_7_out));
  Register #(.width(32)) register_8 (
    .D(ALU_result_EX_MEM), .en(enable8), .Q(Output_ALU_result_EX_MEM), .clk(clock_8_out), .clr(in_24));
  Clock clock_8 (.out(clock_8_out));
  Register #(.width(32)) register_9 (
    .D(Read_data2_EX_MEM), .en(enable9), .Q(Output_Read_data2_EX_MEM), .clk(clock_9_out), .clr(in_27));
  Clock clock_9 (.out(clock_9_out));
  Clock clock_10 (.out(clock_10_out));
  Register #(.width(5)) register_10 (
    .D(Input7_EX_MEM), .en(enable10), .Q(Output7EX_MEM), .clk(clock_10_out), .clr(in_30));
endmodule

module MEM_WB (
  input  WB_MEM_WB1,
  input  enable1,
  input  in_3,
  input  WB_MEM_WB2,
  input  enable5,
  input  in_6,
  input  [31:0] Read_data_MEM_WB,
  input  enable2,
  input  in_9,
  input  [31:0] ALU_result_MEM_WB,
  input  enable3,
  input  in_12,
  input  [4:0] WriteregMuxoutput_MEM_WB,
  input  enable4,
  input  in_15,
  output Output_WB_MEM_WB1,
  output Output_WB_MEM_WB2,
  output [31:0] Read_data_MEM_WB_2,
  output [31:0] Output_ALU_resultMEM_WB,
  output [4:0] Output_WriteregMuxoutput_MEM_WB
);

  wire clock_1_out, clock_2_out, clock_3_out, clock_4_out, clock_5_out;

  Clock clock_1 (.out(clock_1_out));
  Clock clock_2 (.out(clock_2_out));
  Clock clock_3 (.out(clock_3_out));
  Clock clock_4 (.out(clock_4_out));
  Clock clock_5 (.out(clock_5_out));
  Register #(.width(1)) register_1 (.D(WB_MEM_WB1), .en(enable1), .Q(Output_WB_MEM_WB1), .clk(clock_1_out), .clr(in_3));
  Register #(.width(1)) register_2 (.D(WB_MEM_WB2), .en(enable5), .Q(Output_WB_MEM_WB2), .clk(clock_2_out), .clr(in_6));
  Register #(.width(32)) register_3 (
    .D(Read_data_MEM_WB), .en(enable2), .Q(Read_data_MEM_WB_2), .clk(clock_3_out), .clr(in_9));
  Register #(.width(32)) register_4 (
    .D(ALU_result_MEM_WB), .en(enable3), .Q(Output_ALU_resultMEM_WB), .clk(clock_4_out), .clr(in_12));
  Register #(.width(5)) register_5 (
    .D(WriteregMuxoutput_MEM_WB), .en(enable4), .Q(Output_WriteregMuxoutput_MEM_WB), .clk(clock_5_out),
    .clr(in_15));
endmodule
